// Digital circuit Alu.dig as structural Verilog
// Arithmetic logic unit module. Supports addition and subtraction.
module Alu (
  input  [7:0] A,
  input  [7:0] B,
  input  SUBTRACT,
  input  BUS_nOUT,
  output [7:0] BUS,
  output [7:0] OUT,
  output CARRY
);

  wire _74245_1_pin2, _74245_1_pin3, _74245_1_pin4, _74245_1_pin5, _74245_1_pin6, _74245_1_pin7,
       _74245_1_pin8, _74245_1_pin9, B0xor, B1xor, B2xor, B3xor, B4xor, B5xor, B6xor, B7xor, CARRY_OUT,
       LOW_C_OUT;

  xor xor_1 (CARRY, SUBTRACT, CARRY_OUT);
  _74245 _74245_1 (
    .pin1(1'b0), .pin2(_74245_1_pin2), .pin3(_74245_1_pin3), .pin4(_74245_1_pin4), .pin5(_74245_1_pin5),
    .pin6(_74245_1_pin6), .pin7(_74245_1_pin7), .pin8(_74245_1_pin8), .pin9(_74245_1_pin9), .pin10(1'b0),
    .pin11(OUT[7]), .pin12(OUT[6]), .pin13(OUT[5]), .pin14(OUT[4]), .pin15(OUT[3]), .pin16(OUT[2]),
    .pin17(OUT[1]), .pin18(OUT[0]), .pin19(BUS_nOUT), .pin20(1'b1));
  BusSplitter #(.Bits(8)) bussplitter_1 (
    .D(BUS), .OE(BUS_nOUT), .D0(_74245_1_pin2), .D1(_74245_1_pin3), .D2(_74245_1_pin4), .D3(_74245_1_pin5),
    .D4(_74245_1_pin6), .D5(_74245_1_pin7), .D6(_74245_1_pin8), .D7(_74245_1_pin9));
  _74283 _74283_1 (
    .pin1(OUT[5]), .pin2(B5xor), .pin3(A[5]), .pin4(OUT[4]), .pin5(A[4]), .pin6(B4xor), .pin7(LOW_C_OUT),
    .pin8(1'b0), .pin9(CARRY_OUT), .pin10(OUT[7]), .pin11(B7xor), .pin12(A[7]), .pin13(OUT[6]), .pin14(A[6]),
    .pin15(B6xor), .pin16(1'b1));
  _74283 _74283_2 (
    .pin1(OUT[1]), .pin2(B1xor), .pin3(A[1]), .pin4(OUT[0]), .pin5(A[0]), .pin6(B0xor), .pin7(SUBTRACT),
    .pin8(1'b0), .pin9(LOW_C_OUT), .pin10(OUT[3]), .pin11(B3xor), .pin12(A[3]), .pin13(OUT[2]), .pin14(A[2]),
    .pin15(B2xor), .pin16(1'b1));
  _7486 _7486_1 (
    .pin1(B[4]), .pin2(SUBTRACT), .pin3(B4xor), .pin4(B[5]), .pin5(SUBTRACT), .pin6(B5xor), .pin7(1'b0),
    .pin8(B6xor), .pin9(B[6]), .pin10(SUBTRACT), .pin11(B7xor), .pin12(B[7]), .pin13(SUBTRACT), .pin14(1'b1));
  _7486 _7486_2 (
    .pin1(B[0]), .pin2(SUBTRACT), .pin3(B0xor), .pin4(B[1]), .pin5(SUBTRACT), .pin6(B1xor), .pin7(1'b0),
    .pin8(B2xor), .pin9(B[2]), .pin10(SUBTRACT), .pin11(B3xor), .pin12(B[3]), .pin13(SUBTRACT), .pin14(1'b1));

  // Other names for the same wires on the sheet: S0 = OUT[0]; S1 = OUT[1]; S2 = OUT[2]; S3 = OUT[3]; S4 = OUT[4];
  //   S5 = OUT[5]; S6 = OUT[6]; S7 = OUT[7]

  // Notes on the sheet:
  //   BUS_nOUT: default 1
  //   B to A (LOW)
  //   Digital workaround for bus sharing
endmodule
