// Digital circuit Control.dig as structural Verilog
// Control unit module.
module Control (
  input  nCLOCK,
  input  nRESET,
  input  [7:0] IR,
  input  [1:0] FLAGS,
  output HALT,
  output PC_COUNT,
  output ALU_SUBTRACT,
  output OUT_SIGNED_IN,
  output FLAGS_IN,
  output ZERO_BUS_nOUT,
  output RAM_BUS_nOUT,
  output PC_BUS_nOUT,
  output IR_BUS_nOUT,
  output REGA_BUS_nOUT,
  output REGB_BUS_nOUT,
  output ALU_BUS_nOUT,
  output RAM_BUS_nIN,
  output MAR_BUS_nIN,
  output PC_BUS_nIN,
  output IR_BUS_nIN,
  output REGA_BUS_nIN,
  output REGB_BUS_nIN,
  output OUT_BUS_nIN,
  output [2:0] PEEK_STEP,
  output PEEK_LAST_STEP,
  output [3:0] PEEK_INSTRUCTION,
  output [2:0] PEEK_BUS_OUT_ADDRESS,
  output [2:0] PEEK_BUS_IN_ADDRESS,
  output [15:0] PEEK_CONTROL,
  output RESETTING
);

  wire _74161_1_pin9, BUS_OUT_0, BUS_OUT_6;

  // Probe on PEEK_STEP
  _74161 _74161_1 (
    .pin1(nRESET), .pin2(nCLOCK), .pin3(1'b0), .pin4(1'b0), .pin5(1'b0), .pin6(1'b0), .pin7(1'b1),
    .pin8(1'b0), .pin9(_74161_1_pin9), .pin10(1'b1), .pin12(PEEK_STEP[2]), .pin13(PEEK_STEP[1]),
    .pin14(PEEK_STEP[0]), .pin16(1'b1));  // open: pin11, pin15
  JK_FF jk_ff_1 (.J(PEEK_CONTROL[15]), .C(nCLOCK), .K(1'b0), .nQ(RESETTING));  // open: Q
  LED led_1 (.in(IR[0]));
  LED led_2 (.in(IR[1]));
  LED led_3 (.in(IR[2]));
  LED led_4 (.in(IR[3]));
  // Probe on IR[7:4]
  EEPROM #(.AddrBits(15), .Bits(8)) eeprom_1 (
    .A({1'b0, RESETTING, 4'b0000, FLAGS, IR[7:4], PEEK_STEP}), .CS(~1'b0), .WE(~1'b1), .OE(~1'b0),
    .D({PC_COUNT, HALT, PEEK_BUS_IN_ADDRESS, PEEK_BUS_OUT_ADDRESS}));
  EEPROM #(.AddrBits(15), .Bits(8)) eeprom_2 (
    .A({1'b1, RESETTING, 4'b0000, FLAGS, IR[7:4], PEEK_STEP}), .CS(~1'b0), .WE(~1'b1), .OE(~1'b0),
    .D({PEEK_CONTROL[15:11], FLAGS_IN, OUT_SIGNED_IN, ALU_SUBTRACT}));
  not not_1 (_74161_1_pin9, PEEK_CONTROL[15]);
  // Probe on {RESETTING, 4'b0000, FLAGS, IR[7:4], PEEK_STEP}
  // Probe on {PC_COUNT, HALT, PEEK_BUS_IN_ADDRESS, PEEK_BUS_OUT_ADDRESS}
  // Probe on {PEEK_CONTROL[15:11], FLAGS_IN, OUT_SIGNED_IN, ALU_SUBTRACT}
  and and_1 (ZERO_BUS_nOUT, BUS_OUT_0, BUS_OUT_6);
  _74138 BUS_OUT_ADDRESS (
    .pin1(PEEK_BUS_OUT_ADDRESS[0]), .pin2(PEEK_BUS_OUT_ADDRESS[1]), .pin3(PEEK_BUS_OUT_ADDRESS[2]),
    .pin4(1'b0), .pin5(1'b0), .pin6(1'b1), .pin7(BUS_OUT_6), .pin8(1'b0), .pin9(ALU_BUS_nOUT),
    .pin10(REGB_BUS_nOUT), .pin11(REGA_BUS_nOUT), .pin12(IR_BUS_nOUT), .pin13(PC_BUS_nOUT),
    .pin14(RAM_BUS_nOUT), .pin15(BUS_OUT_0), .pin16(1'b1));
  // Probe on PEEK_BUS_OUT_ADDRESS
  _74138 BUS_IN_ADDRESS (
    .pin1(PEEK_BUS_IN_ADDRESS[0]), .pin2(PEEK_BUS_IN_ADDRESS[1]), .pin3(PEEK_BUS_IN_ADDRESS[2]), .pin4(1'b0),
    .pin5(1'b0), .pin6(1'b1), .pin7(OUT_BUS_nIN), .pin8(1'b0), .pin9(REGB_BUS_nIN), .pin10(REGA_BUS_nIN),
    .pin11(IR_BUS_nIN), .pin12(PC_BUS_nIN), .pin13(MAR_BUS_nIN), .pin14(RAM_BUS_nIN), .pin16(1'b1));  // open: pin15
  // Probe on PEEK_BUS_IN_ADDRESS

  assign PEEK_CONTROL[10:0] = {FLAGS_IN, OUT_SIGNED_IN, ALU_SUBTRACT, PC_COUNT, HALT, PEEK_BUS_IN_ADDRESS, PEEK_BUS_OUT_ADDRESS};
  assign PEEK_INSTRUCTION = IR[7:4];
  assign PEEK_LAST_STEP = PEEK_CONTROL[15];

  // Other names for the same wires on the sheet: ADDRESS (some bits) = {RESETTING, FLAGS, IR[7:4], PEEK_STEP};
  //   STEP[2:0] = PEEK_STEP; CONTROL_HIGH[7:0] = {PEEK_CONTROL[15:11], FLAGS_IN, OUT_SIGNED_IN, ALU_SUBTRACT};
  //   LAST_STEP = PEEK_CONTROL[15]; BUS_OUT_ADDRESS[2:0] = PEEK_BUS_OUT_ADDRESS;
  //   CONTROL_LOW[7:0] = {PC_COUNT, HALT, PEEK_BUS_IN_ADDRESS, PEEK_BUS_OUT_ADDRESS};
  //   BUS_IN_ADDRESS[2:0] = PEEK_BUS_IN_ADDRESS; IR_HIGH[3:0] = IR[7:4]

  // Notes on the sheet:
  //   nRESET: default 1
  //   contents of eeprom_1 (hex, n*v repeats v):
  //   12,a1,0,0,0,0,0,0,12,a1,13,29,0,0,0,0,12,a1,13,31,2e,0,0,0,12,a1,13,31,2e,0,0,0,12,
  //   a1,13,c,0,0,0,0,12,a1,2b,0,0,0,0,0,12,a1,1b,0,0,0,0,0,12,a1,0,0,0,0,0,0,12,a1,0,0,
  //   0,0,0,0,12,a1,0,0,0,0,0,0,12,a1,0,0,0,0,0,0,12,a1,0,0,0,0,0,0,12,a1,0,0,0,0,0,0,12,
  //   a1,0,0,0,0,0,0,12,a1,3c,0,0,0,0,0,12,a1,40,0,0,0,0,0,12,a1,0,0,0,0,0,0,12,a1,13,29,
  //   0,0,0,0,12,a1,13,31,2e,0,0,0,12,a1,13,31,2e,0,0,0,12,a1,13,c,0,0,0,0,12,a1,2b,0,0,
  //   0,0,0,12,a1,1b,0,0,0,0,0,12,a1,1b,0,0,0,0,0,12,a1,0,0,0,0,0,0,12,a1,0,0,0,0,0,0,12,
  //   a1,0,0,0,0,0,0,12,a1,0,0,0,0,0,0,12,a1,0,0,0,0,0,0,12,a1,0,0,0,0,0,0,12,a1,3c,0,0,
  //   0,0,0,12,a1,40,0,0,0,0,0,12,a1,0,0,0,0,0,0,12,a1,13,29,0,0,0,0,12,a1,13,31,2e,0,0,
  //   0,12,a1,13,31,2e,0,0,0,12,a1,13,c,0,0,0,0,12,a1,2b,0,0,0,0,0,12,a1,1b,0,0,0,0,0,12,
  //   a1,0,0,0,0,0,0,12,a1,1b,0,0,0,0,0,12,a1,0,0,0,0,0,0,12,a1,0,0,0,0,0,0,12,a1,0,0,0,
  //   0,0,0,12,a1,0,0,0,0,0,0,12,a1,0,0,0,0,0,0,12,a1,3c,0,0,0,0,0,12,a1,40,0,0,0,0,0,12,
  //   a1,0,0,0,0,0,0,12,a1,13,29,0,0,0,0,12,a1,13,31,2e,0,0,0,12,a1,13,31,2e,0,0,0,12,a1,
  //   13,c,0,0,0,0,12,a1,2b,0,0,0,0,0,12,a1,1b,0,0,0,0,0,12,a1,1b,0,0,0,0,0,12,a1,1b,0,
  //   0,0,0,0,12,a1,0,0,0,0,0,0,12,a1,0,0,0,0,0,0,12,a1,0,0,0,0,0,0,12,a1,0,0,0,0,0,0,12,
  //   a1,0,0,0,0,0,0,12,a1,3c,0,0,0,0,0,12,a1,40,0,0,0,0,0,12,a1,0,0,0,0,0,0,12,a1,13,29,
  //   0,0,0,0,12,a1,13,31,2e,0,0,0,12,a1,13,31,2e,0,0,0,12,a1,13,c,0,0,0,0,12,a1,2b,0,0,
  //   0,0,0,12,a1,1b,0,0,0,0,0,12,a1,0,0,0,0,0,0,12,a1,0,0,0,0,0,0,12,a1,0,0,0,0,0,0,12,
  //   a1,0,0,0,0,0,0,12,a1,0,0,0,0,0,0,12,a1,0,0,0,0,0,0,12,a1,0,0,0,0,0,0,12,a1,3c,0,0,
  //   0,0,0,12,a1,40,0,0,0,0,0,12,a1,0,0,0,0,0,0,12,a1,13,29,0,0,0,0,12,a1,13,31,2e,0,0,
  //   0,12,a1,13,31,2e,0,0,0,12,a1,13,c,0,0,0,0,12,a1,2b,0,0,0,0,0,12,a1,1b,0,0,0,0,0,12,
  //   a1,1b,0,0,0,0,0,12,a1,0,0,0,0,0,0,12,a1,0,0,0,0,0,0,12,a1,0,0,0,0,0,0,12,a1,0,0,0,
  //   0,0,0,12,a1,0,0,0,0,0,0,12,a1,0,0,0,0,0,0,12,a1,3c,0,0,0,0,0,12,a1,40,0,0,0,0,0,12,
  //   a1,0,0,0,0,0,0,12,a1,13,29,0,0,0,0,12,a1,13,31,2e,0,0,0,12,a1,13,31,2e,0,0,0,12,a1,
  //   13,c,0,0,0,0,12,a1,2b,0,0,0,0,0,12,a1,1b,0,0,0,0,0,12,a1,0,0,0,0,0,0,12,a1,1b,0,0,
  //   0,0,0,12,a1,0,0,0,0,0,0,12,a1,0,0,0,0,0,0,12,a1,0,0,0,0,0,0,12,a1,0,0,0,0,0,0,12,
  //   a1,0,0,0,0,0,0,12,a1,3c,0,0,0,0,0,12,a1,40,0,0,0,0,0,12,a1,0,0,0,0,0,0,12,a1,13,29,
  //   0,0,0,0,12,a1,13,31,2e,0,0,0,12,a1,13,31,2e,0,0,0,12,a1,13,c,0,0,0,0,12,a1,2b,0,0,
  //   0,0,0,12,a1,1b,0,0,0,0,0,12,a1,1b,0,0,0,0,0,12,a1,1b,0,0,0,0,0,12,a1,0,0,0,0,0,0,
  //   12,a1,0,0,0,0,0,0,12,a1,0,0,0,0,0,0,12,a1,0,0,0,0,0,0,12,a1,0,0,0,0,0,0,12,a1,3c,
  //   0,0,0,0,0,12,a1,40,0,0,0,0,0,12,a1,0,0,0,0,0,0,12,a1,13,29,0,0,0,0,12,a1,13,31,2e,
  //   0,0,0,12,a1,13,31,2e,0,0,0,12,a1,13,c,0,0,0,0,12,a1,2b,0,0,0,0,0,12,a1,1b,0,0,0,0,
  //   0,12,a1,0,0,0,0,0,0,12,a1,0,0,0,0,0,0,12,a1,0,0,0,0,0,0,12,a1,0,0,0,0,0,0,12,a1,0,
  //   0,0,0,0,0,12,a1,0,0,0,0,0,0,12,a1,0,0,0,0,0,0,12,a1,3c,0,0,0,0,0,12,a1,40,0,0,0,0,
  //   0,12,a1,0,0,0,0,0,0,12,a1,13,29,0,0,0,0,12,a1,13,31,2e,0,0,0,12,a1,13,31,2e,0,0,0,
  //   12,a1,13,c,0,0,0,0,12,a1,2b,0,0,0,0,0,12,a1,1b,0,0,0,0,0,12,a1,1b,0,0,0,0,0,12,a1,
  //   0,0,0,0,0,0,12,a1,0,0,0,0,0,0,12,a1,0,0,0,0,0,0,12,a1,0,0,0,0,0,0,12,a1,0,0,0,0,0,
  //   0,12,a1,0,0,0,0,0,0,12,a1,3c,0,0,0,0,0,12,a1,40,0,0,0,0,0,12,a1,0,0,0,0,0,0,12,a1,
  //   13,29,0,0,0,0,12,a1,13,31,2e,0,0,0,12,a1,13,31,2e,0,0,0,12,a1,13,c,0,0,0,0,12,a1,
  //   2b,0,0,0,0,0,12,a1,1b,0,0,0,0,0,12,a1,0,0,0,0,0,0,12,a1,1b,0,0,0,0,0,12,a1,0,0,0,
  //   0,0,0,12,a1,0,0,0,0,0,0,12,a1,0,0,0,0,0,0,12,a1,0,0,0,0,0,0,12,a1,0,0,0,0,0,0,12,
  //   a1,3c,0,0,0,0,0,12,a1,40,0,0,0,0,0,12,a1,0,0,0,0,0,0,12,a1,13,29,0,0,0,0,12,a1,13,
  //   31,2e,0,0,0,12,a1,13,31,2e,0,0,0,12,a1,13,c,0,0,0,0,12,a1,2b,0,0,0,0,0,12,a1,1b,0,
  //   0,0,0,0,12,a1,1b,0,0,0,0,0,12,a1,1b,0,0,0,0,0,12,a1,0,0,0,0,0,0,12,a1,0,0,0,0,0,0,
  //   12,a1,0,0,0,0,0,0,12,a1,0,0,0,0,0,0,12,a1,0,0,0,0,0,0,12,a1,3c,0,0,0,0,0,12,a1,40,
  //   0,0,0,0,0,12,a1,0,0,0,0,0,0,12,a1,13,29,0,0,0,0,12,a1,13,31,2e,0,0,0,12,a1,13,31,
  //   2e,0,0,0,12,a1,13,c,0,0,0,0,12,a1,2b,0,0,0,0,0,12,a1,1b,0,0,0,0,0,12,a1,0,0,0,0,0,
  //   0,12,a1,0,0,0,0,0,0,12,a1,0,0,0,0,0,0,12,a1,0,0,0,0,0,0,12,a1,0,0,0,0,0,0,12,a1,0,
  //   0,0,0,0,0,12,a1,0,0,0,0,0,0,12,a1,3c,0,0,0,0,0,12,a1,40,0,0,0,0,0,12,a1,0,0,0,0,0,
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  //   contents of eeprom_2 (hex, n*v repeats v):
  //   12,a1,0,0,0,0,0,0,12,a1,13,29,0,0,0,0,12,a1,13,31,2e,0,0,0,12,a1,13,31,2e,0,0,0,12,
  //   a1,13,c,0,0,0,0,12,a1,2b,0,0,0,0,0,12,a1,1b,0,0,0,0,0,12,a1,0,0,0,0,0,0,12,a1,0,0,
  //   0,0,0,0,12,a1,0,0,0,0,0,0,12,a1,0,0,0,0,0,0,12,a1,0,0,0,0,0,0,12,a1,0,0,0,0,0,0,12,
  //   a1,0,0,0,0,0,0,12,a1,3c,0,0,0,0,0,12,a1,40,0,0,0,0,0,12,a1,0,0,0,0,0,0,12,a1,13,29,
  //   0,0,0,0,12,a1,13,31,2e,0,0,0,12,a1,13,31,2e,0,0,0,12,a1,13,c,0,0,0,0,12,a1,2b,0,0,
  //   0,0,0,12,a1,1b,0,0,0,0,0,12,a1,1b,0,0,0,0,0,12,a1,0,0,0,0,0,0,12,a1,0,0,0,0,0,0,12,
  //   a1,0,0,0,0,0,0,12,a1,0,0,0,0,0,0,12,a1,0,0,0,0,0,0,12,a1,0,0,0,0,0,0,12,a1,3c,0,0,
  //   0,0,0,12,a1,40,0,0,0,0,0,12,a1,0,0,0,0,0,0,12,a1,13,29,0,0,0,0,12,a1,13,31,2e,0,0,
  //   0,12,a1,13,31,2e,0,0,0,12,a1,13,c,0,0,0,0,12,a1,2b,0,0,0,0,0,12,a1,1b,0,0,0,0,0,12,
  //   a1,0,0,0,0,0,0,12,a1,1b,0,0,0,0,0,12,a1,0,0,0,0,0,0,12,a1,0,0,0,0,0,0,12,a1,0,0,0,
  //   0,0,0,12,a1,0,0,0,0,0,0,12,a1,0,0,0,0,0,0,12,a1,3c,0,0,0,0,0,12,a1,40,0,0,0,0,0,12,
  //   a1,0,0,0,0,0,0,12,a1,13,29,0,0,0,0,12,a1,13,31,2e,0,0,0,12,a1,13,31,2e,0,0,0,12,a1,
  //   13,c,0,0,0,0,12,a1,2b,0,0,0,0,0,12,a1,1b,0,0,0,0,0,12,a1,1b,0,0,0,0,0,12,a1,1b,0,
  //   0,0,0,0,12,a1,0,0,0,0,0,0,12,a1,0,0,0,0,0,0,12,a1,0,0,0,0,0,0,12,a1,0,0,0,0,0,0,12,
  //   a1,0,0,0,0,0,0,12,a1,3c,0,0,0,0,0,12,a1,40,0,0,0,0,0,12,a1,0,0,0,0,0,0,12,a1,13,29,
  //   0,0,0,0,12,a1,13,31,2e,0,0,0,12,a1,13,31,2e,0,0,0,12,a1,13,c,0,0,0,0,12,a1,2b,0,0,
  //   0,0,0,12,a1,1b,0,0,0,0,0,12,a1,0,0,0,0,0,0,12,a1,0,0,0,0,0,0,12,a1,0,0,0,0,0,0,12,
  //   a1,0,0,0,0,0,0,12,a1,0,0,0,0,0,0,12,a1,0,0,0,0,0,0,12,a1,0,0,0,0,0,0,12,a1,3c,0,0,
  //   0,0,0,12,a1,40,0,0,0,0,0,12,a1,0,0,0,0,0,0,12,a1,13,29,0,0,0,0,12,a1,13,31,2e,0,0,
  //   0,12,a1,13,31,2e,0,0,0,12,a1,13,c,0,0,0,0,12,a1,2b,0,0,0,0,0,12,a1,1b,0,0,0,0,0,12,
  //   a1,1b,0,0,0,0,0,12,a1,0,0,0,0,0,0,12,a1,0,0,0,0,0,0,12,a1,0,0,0,0,0,0,12,a1,0,0,0,
  //   0,0,0,12,a1,0,0,0,0,0,0,12,a1,0,0,0,0,0,0,12,a1,3c,0,0,0,0,0,12,a1,40,0,0,0,0,0,12,
  //   a1,0,0,0,0,0,0,12,a1,13,29,0,0,0,0,12,a1,13,31,2e,0,0,0,12,a1,13,31,2e,0,0,0,12,a1,
  //   13,c,0,0,0,0,12,a1,2b,0,0,0,0,0,12,a1,1b,0,0,0,0,0,12,a1,0,0,0,0,0,0,12,a1,1b,0,0,
  //   0,0,0,12,a1,0,0,0,0,0,0,12,a1,0,0,0,0,0,0,12,a1,0,0,0,0,0,0,12,a1,0,0,0,0,0,0,12,
  //   a1,0,0,0,0,0,0,12,a1,3c,0,0,0,0,0,12,a1,40,0,0,0,0,0,12,a1,0,0,0,0,0,0,12,a1,13,29,
  //   0,0,0,0,12,a1,13,31,2e,0,0,0,12,a1,13,31,2e,0,0,0,12,a1,13,c,0,0,0,0,12,a1,2b,0,0,
  //   0,0,0,12,a1,1b,0,0,0,0,0,12,a1,1b,0,0,0,0,0,12,a1,1b,0,0,0,0,0,12,a1,0,0,0,0,0,0,
  //   12,a1,0,0,0,0,0,0,12,a1,0,0,0,0,0,0,12,a1,0,0,0,0,0,0,12,a1,0,0,0,0,0,0,12,a1,3c,
  //   0,0,0,0,0,12,a1,40,0,0,0,0,0,12,a1,0,0,0,0,0,0,12,a1,13,29,0,0,0,0,12,a1,13,31,2e,
  //   0,0,0,12,a1,13,31,2e,0,0,0,12,a1,13,c,0,0,0,0,12,a1,2b,0,0,0,0,0,12,a1,1b,0,0,0,0,
  //   0,12,a1,0,0,0,0,0,0,12,a1,0,0,0,0,0,0,12,a1,0,0,0,0,0,0,12,a1,0,0,0,0,0,0,12,a1,0,
  //   0,0,0,0,0,12,a1,0,0,0,0,0,0,12,a1,0,0,0,0,0,0,12,a1,3c,0,0,0,0,0,12,a1,40,0,0,0,0,
  //   0,12,a1,0,0,0,0,0,0,12,a1,13,29,0,0,0,0,12,a1,13,31,2e,0,0,0,12,a1,13,31,2e,0,0,0,
  //   12,a1,13,c,0,0,0,0,12,a1,2b,0,0,0,0,0,12,a1,1b,0,0,0,0,0,12,a1,1b,0,0,0,0,0,12,a1,
  //   0,0,0,0,0,0,12,a1,0,0,0,0,0,0,12,a1,0,0,0,0,0,0,12,a1,0,0,0,0,0,0,12,a1,0,0,0,0,0,
  //   0,12,a1,0,0,0,0,0,0,12,a1,3c,0,0,0,0,0,12,a1,40,0,0,0,0,0,12,a1,0,0,0,0,0,0,12,a1,
  //   13,29,0,0,0,0,12,a1,13,31,2e,0,0,0,12,a1,13,31,2e,0,0,0,12,a1,13,c,0,0,0,0,12,a1,
  //   2b,0,0,0,0,0,12,a1,1b,0,0,0,0,0,12,a1,0,0,0,0,0,0,12,a1,1b,0,0,0,0,0,12,a1,0,0,0,
  //   0,0,0,12,a1,0,0,0,0,0,0,12,a1,0,0,0,0,0,0,12,a1,0,0,0,0,0,0,12,a1,0,0,0,0,0,0,12,
  //   a1,3c,0,0,0,0,0,12,a1,40,0,0,0,0,0,12,a1,0,0,0,0,0,0,12,a1,13,29,0,0,0,0,12,a1,13,
  //   31,2e,0,0,0,12,a1,13,31,2e,0,0,0,12,a1,13,c,0,0,0,0,12,a1,2b,0,0,0,0,0,12,a1,1b,0,
  //   0,0,0,0,12,a1,1b,0,0,0,0,0,12,a1,1b,0,0,0,0,0,12,a1,0,0,0,0,0,0,12,a1,0,0,0,0,0,0,
  //   12,a1,0,0,0,0,0,0,12,a1,0,0,0,0,0,0,12,a1,0,0,0,0,0,0,12,a1,3c,0,0,0,0,0,12,a1,40,
  //   0,0,0,0,0,12,a1,0,0,0,0,0,0,12,a1,13,29,0,0,0,0,12,a1,13,31,2e,0,0,0,12,a1,13,31,
  //   2e,0,0,0,12,a1,13,c,0,0,0,0,12,a1,2b,0,0,0,0,0,12,a1,1b,0,0,0,0,0,12,a1,0,0,0,0,0,
  //   0,12,a1,0,0,0,0,0,0,12,a1,0,0,0,0,0,0,12,a1,0,0,0,0,0,0,12,a1,0,0,0,0,0,0,12,a1,0,
  //   0,0,0,0,0,12,a1,0,0,0,0,0,0,12,a1,3c,0,0,0,0,0,12,a1,40,0,0,0,0,0,12,a1,0,0,0,0,0,
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endmodule
