// Digital circuit Flags.dig as structural Verilog
module Flags (
  input  CLOCK,
  input  RESET,
  input  FLAGS_IN,
  input  [7:0] ALU,
  input  ALU_CARRY,
  output CARRY_FLAG,
  output ZERO_FLAG
);

  wire ALU_nZERO, ALU_ZERO, FLAGS_nIN;

  DiodeForward diodeforward_1 (.in(ALU[0]), .out(ALU_nZERO));
  DiodeForward diodeforward_2 (.in(ALU[1]), .out(ALU_nZERO));
  DiodeForward diodeforward_3 (.in(ALU[2]), .out(ALU_nZERO));
  DiodeForward diodeforward_4 (.in(ALU[3]), .out(ALU_nZERO));
  DiodeForward diodeforward_5 (.in(ALU[4]), .out(ALU_nZERO));
  DiodeForward diodeforward_6 (.in(ALU[5]), .out(ALU_nZERO));
  DiodeForward diodeforward_7 (.in(ALU[6]), .out(ALU_nZERO));
  DiodeForward diodeforward_8 (.in(ALU[7]), .out(ALU_nZERO));
  PullDown pulldown_1 (.out(ALU_nZERO));
  _7404 _7404_1 (
    .pin1(ALU_nZERO), .pin2(ALU_ZERO), .pin3(1'b0), .pin5(1'b0), .pin7(1'b0), .pin9(1'b0), .pin10(FLAGS_nIN),
    .pin11(FLAGS_IN), .pin13(1'b0), .pin14(1'b1));  // open: pin4, pin6, pin8, pin12
  _74173 _74173_1 (
    .pin1(1'b0), .pin2(1'b0), .pin3(CARRY_FLAG), .pin4(ZERO_FLAG), .pin7(CLOCK), .pin8(1'b0),
    .pin9(FLAGS_nIN), .pin10(FLAGS_nIN), .pin11(1'b0), .pin12(1'b0), .pin13(ALU_ZERO), .pin14(ALU_CARRY),
    .pin15(RESET), .pin16(1'b1));  // open: pin5, pin6
endmodule
