// Digital circuit Mar.dig as structural Verilog
// Memory address register module.
module Mar (
  input  CLOCK,
  input  RESET,
  input  [7:0] BUS,
  input  BUS_nIN,
  output [7:0] OUT
);

  _74173 _74173_1 (
    .pin1(1'b0), .pin2(1'b0), .pin3(OUT[4]), .pin4(OUT[5]), .pin5(OUT[6]), .pin6(OUT[7]), .pin7(CLOCK),
    .pin8(1'b0), .pin9(BUS_nIN), .pin10(BUS_nIN), .pin11(BUS[7]), .pin12(BUS[6]), .pin13(BUS[5]),
    .pin14(BUS[4]), .pin15(RESET), .pin16(1'b1));
  _74173 _74173_2 (
    .pin1(1'b0), .pin2(1'b0), .pin3(OUT[0]), .pin4(OUT[1]), .pin5(OUT[2]), .pin6(OUT[3]), .pin7(CLOCK),
    .pin8(1'b0), .pin9(BUS_nIN), .pin10(BUS_nIN), .pin11(BUS[3]), .pin12(BUS[2]), .pin13(BUS[1]),
    .pin14(BUS[0]), .pin15(RESET), .pin16(1'b1));

  // Other names for the same wires on the sheet: D0 = BUS[0]; D1 = BUS[1]; D2 = BUS[2]; D3 = BUS[3]; D4 = BUS[4];
  //   D5 = BUS[5]; D6 = BUS[6]; D7 = BUS[7]; Q0 = OUT[0]; Q1 = OUT[1]; Q2 = OUT[2]; Q3 = OUT[3]; Q4 = OUT[4];
  //   Q5 = OUT[5]; Q6 = OUT[6]; Q7 = OUT[7]

  // Notes on the sheet:
  //   RESET: default 1
  //   BUS_nIN: default 1
endmodule
