// Digital circuit Pc.dig as structural Verilog
// Program Counter module.
module Pc (
  input  CLOCK,
  input  nRESET,
  input  COUNT,
  input  BUS_nIN,
  input  BUS_nOUT,
  output [7:0] BUS,
  output [7:0] PEEK
);

  wire _74161_1_pin10, _74245_1_pin2, _74245_1_pin3, _74245_1_pin4, _74245_1_pin5, _74245_1_pin6,
       _74245_1_pin7, _74245_1_pin8, _74245_1_pin9;

  _74245 _74245_1 (
    .pin1(1'b0), .pin2(_74245_1_pin2), .pin3(_74245_1_pin3), .pin4(_74245_1_pin4), .pin5(_74245_1_pin5),
    .pin6(_74245_1_pin6), .pin7(_74245_1_pin7), .pin8(_74245_1_pin8), .pin9(_74245_1_pin9), .pin10(1'b0),
    .pin11(PEEK[7]), .pin12(PEEK[6]), .pin13(PEEK[5]), .pin14(PEEK[4]), .pin15(PEEK[3]), .pin16(PEEK[2]),
    .pin17(PEEK[1]), .pin18(PEEK[0]), .pin19(BUS_nOUT), .pin20(1'b1));
  BusSplitter #(.Bits(8)) bussplitter_1 (
    .D(BUS), .OE(BUS_nOUT), .D0(_74245_1_pin2), .D1(_74245_1_pin3), .D2(_74245_1_pin4), .D3(_74245_1_pin5),
    .D4(_74245_1_pin6), .D5(_74245_1_pin7), .D6(_74245_1_pin8), .D7(_74245_1_pin9));
  _74161 _74161_1 (
    .pin1(nRESET), .pin2(CLOCK), .pin3(BUS[4]), .pin4(BUS[5]), .pin5(BUS[6]), .pin6(BUS[7]), .pin7(COUNT),
    .pin8(1'b0), .pin9(BUS_nIN), .pin10(_74161_1_pin10), .pin11(PEEK[7]), .pin12(PEEK[6]), .pin13(PEEK[5]),
    .pin14(PEEK[4]), .pin16(1'b1));  // open: pin15
  _74161 _74161_2 (
    .pin1(nRESET), .pin2(CLOCK), .pin3(BUS[0]), .pin4(BUS[1]), .pin5(BUS[2]), .pin6(BUS[3]), .pin7(COUNT),
    .pin8(1'b0), .pin9(BUS_nIN), .pin10(1'b1), .pin11(PEEK[3]), .pin12(PEEK[2]), .pin13(PEEK[1]),
    .pin14(PEEK[0]), .pin15(_74161_1_pin10), .pin16(1'b1));

  // Other names for the same wires on the sheet: A_LOW = BUS[0]; B_LOW = BUS[1]; C_LOW = BUS[2]; D_LOW = BUS[3];
  //   A_HIGH = BUS[4]; B_HIGH = BUS[5]; C_HIGH = BUS[6]; D_HIGH = BUS[7]; Q0 = PEEK[0]; Q1 = PEEK[1]; Q2 = PEEK[2];
  //   Q3 = PEEK[3]; Q4 = PEEK[4]; Q5 = PEEK[5]; Q6 = PEEK[6]; Q7 = PEEK[7]; RESET = nRESET

  // Notes on the sheet:
  //   BUS_nIN: default 1
  //   BUS_nOUT: default 1
  //   B to A (LOW)
  //   Digital workaround for bus sharing
endmodule
