// Digital circuit Ram.dig as structural Verilog
// RAM module.
module Ram (
  input  CLOCK,
  input  [7:0] ADDRESS,
  input  BUS_nIN,
  input  BUS_nOUT,
  output [7:0] BUS,
  output [7:0] PEEK
);

  wire _74245_1_pin11, _74245_1_pin12, _74245_1_pin13, _74245_1_pin14, _74245_1_pin15, _74245_1_pin16,
       _74245_1_pin17, _74245_1_pin18, _74245_1_pin19, BUS_IN, CLOCK_WRITE, jk_ff_1_nq, nand_1_out,
       nand_2_out, nand_3_out, not_1_out, not_3_out, not_4_out;

  not not_1 (not_1_out, CLOCK);
  not not_2 (BUS_IN, BUS_nIN);
  not not_3 (not_3_out, not_1_out);
  not not_4 (not_4_out, not_3_out);
  nand nand_1 (nand_1_out, CLOCK, not_4_out);
  _74245 _74245_1 (
    .pin1(BUS_nIN), .pin2(PEEK[7]), .pin3(PEEK[6]), .pin4(PEEK[5]), .pin5(PEEK[4]), .pin6(PEEK[3]),
    .pin7(PEEK[2]), .pin8(PEEK[1]), .pin9(PEEK[0]), .pin10(1'b0), .pin11(_74245_1_pin11),
    .pin12(_74245_1_pin12), .pin13(_74245_1_pin13), .pin14(_74245_1_pin14), .pin15(_74245_1_pin15),
    .pin16(_74245_1_pin16), .pin17(_74245_1_pin17), .pin18(_74245_1_pin18), .pin19(_74245_1_pin19),
    .pin20(1'b1));
  not not_5 (CLOCK_WRITE, nand_1_out);
  nand nand_2 (nand_2_out, BUS_nIN, BUS_nOUT);
  not not_6 (_74245_1_pin19, nand_2_out);
  // Probe CLOCK_WRITE on CLOCK_WRITE
  BusSplitter #(.Bits(8)) bussplitter_1 (
    .D(BUS), .OE(BUS_nOUT), .D0(_74245_1_pin11), .D1(_74245_1_pin12), .D2(_74245_1_pin13),
    .D3(_74245_1_pin14), .D4(_74245_1_pin15), .D5(_74245_1_pin16), .D6(_74245_1_pin17), .D7(_74245_1_pin18));
  nand nand_3 (nand_3_out, CLOCK_WRITE, BUS_IN);
  PullDown pulldown_1 (.out(nand_3_out));
  // Probe RAM ~WE on nand_3_out
  A623308A2WithProgramMemory a623308a2withprogrammemory_1 (
    .A0(ADDRESS[0]), .A1(ADDRESS[1]), .A2(ADDRESS[2]), .A3(ADDRESS[3]), .A4(ADDRESS[4]), .A5(ADDRESS[5]),
    .A6(ADDRESS[6]), .A7(ADDRESS[7]), .A8(1'b0), .A9(1'b0), .A10(1'b0), .A11(1'b0), .A12(jk_ff_1_nq),
    .nCE(1'b0), .nOE(BUS_IN), .nWE(nand_3_out), .D0(PEEK[0]), .D1(PEEK[1]), .D2(PEEK[2]), .D3(PEEK[3]),
    .D4(PEEK[4]), .D5(PEEK[5]), .D6(PEEK[6]), .D7(PEEK[7]), .VCC(1'b1), .GND(1'b0));
  JK_FF jk_ff_1 (.J(CLOCK), .C(CLOCK), .K(1'b0), .nQ(jk_ff_1_nq));  // open: Q

  // Other names for the same wires on the sheet: IN_OUT_D0 = PEEK[0]; IN_OUT_D1 = PEEK[1]; IN_OUT_D2 = PEEK[2];
  //   IN_OUT_D3 = PEEK[3]; IN_OUT_D4 = PEEK[4]; IN_OUT_D5 = PEEK[5]; IN_OUT_D6 = PEEK[6]; IN_OUT_D7 = PEEK[7]

  // Notes on the sheet:
  //   BUS_nIN: default 1
  //   BUS_nOUT: default 1
  //   Digital workaround for bus sharing
  //   Digital workaround. Byte at start address is sometimes not read from program memory. Instead defaulted to 0. This will destroy one byte in an unused region
endmodule
