// Digital circuit Register.dig as structural Verilog
// Register module.
module Register (
  input  CLOCK,
  input  nIN_BUS,
  input  nOUT_BUS,
  output [7:0] BUS,
  output [7:0] OUTPUT
);

  wire _74245_1_pin2, _74245_1_pin3, _74245_1_pin4, _74245_1_pin5, _74245_1_pin6, _74245_1_pin7,
       _74245_1_pin8, _74245_1_pin9;

  _74245 _74245_1 (
    .pin1(1'b0), .pin2(_74245_1_pin2), .pin3(_74245_1_pin3), .pin4(_74245_1_pin4), .pin5(_74245_1_pin5),
    .pin6(_74245_1_pin6), .pin7(_74245_1_pin7), .pin8(_74245_1_pin8), .pin9(_74245_1_pin9), .pin10(1'b0),
    .pin11(OUTPUT[7]), .pin12(OUTPUT[6]), .pin13(OUTPUT[5]), .pin14(OUTPUT[4]), .pin15(OUTPUT[3]),
    .pin16(OUTPUT[2]), .pin17(OUTPUT[1]), .pin18(OUTPUT[0]), .pin19(nOUT_BUS), .pin20(1'b1));
  BusSplitter #(.Bits(8)) bussplitter_1 (
    .D(BUS), .OE(nOUT_BUS), .D0(_74245_1_pin2), .D1(_74245_1_pin3), .D2(_74245_1_pin4), .D3(_74245_1_pin5),
    .D4(_74245_1_pin6), .D5(_74245_1_pin7), .D6(_74245_1_pin8), .D7(_74245_1_pin9));
  _74377 _74377_1 (
    .pin1(nIN_BUS), .pin2(OUTPUT[0]), .pin3(BUS[0]), .pin4(BUS[1]), .pin5(OUTPUT[1]), .pin6(OUTPUT[2]),
    .pin7(BUS[2]), .pin8(BUS[3]), .pin9(OUTPUT[3]), .pin10(1'b0), .pin11(CLOCK), .pin12(OUTPUT[4]),
    .pin13(BUS[4]), .pin14(BUS[5]), .pin15(OUTPUT[5]), .pin16(OUTPUT[6]), .pin17(BUS[6]), .pin18(BUS[7]),
    .pin19(OUTPUT[7]), .pin20(1'b1));

  // Other names for the same wires on the sheet: D0 = BUS[0]; D1 = BUS[1]; D2 = BUS[2]; D3 = BUS[3]; D4 = BUS[4];
  //   D5 = BUS[5]; D6 = BUS[6]; D7 = BUS[7]; Q0 = OUTPUT[0]; Q1 = OUTPUT[1]; Q2 = OUTPUT[2]; Q3 = OUTPUT[3];
  //   Q4 = OUTPUT[4]; Q5 = OUTPUT[5]; Q6 = OUTPUT[6]; Q7 = OUTPUT[7]

  // Notes on the sheet:
  //   nIN_BUS: default 1
  //   nOUT_BUS: default 1
  //   B to A (LOW)
  //   Digital workaround for bus sharing
endmodule
