// Digital circuit A623308A2WithProgramMemory.dig as structural Verilog
// 8K X 8 BIT CMOS SRAM
module A623308A2WithProgramMemory (
  input  A0,
  input  A1,
  input  A2,
  input  A3,
  input  A4,
  input  A5,
  input  A6,
  input  A7,
  input  A8,
  input  A9,
  input  A10,
  input  A11,
  input  A12,
  input  nCE,
  input  nOE,
  input  nWE,
  input  VCC,
  input  GND,
  output D0,
  output D1,
  output D2,
  output D3,
  output D4,
  output D5,
  output D6,
  output D7
);

  wire nor_1_out;
  wire [7:0] ramsingleportsel_d;

  PowerSupply powersupply_1 (.VDD(VCC), .GND(GND));
  RAMSinglePortSel #(.AddrBits(13), .isProgramMemory("true"), .Bits(8)) ramsingleportsel (
    .A({A12, A11, A10, A9, A8, A7, A6, A5, A4, A3, A2, A1, A0}), .CS(~nCE), .WE(~nWE), .OE(~nOE),
    .D(ramsingleportsel_d));
  nor nor_1 (nor_1_out, nCE, ~nWE, nOE);  // NOr
  BusSplitter #(.Bits(8)) bussplitter_1 (
    .D(ramsingleportsel_d), .OE(nor_1_out), .D0(D0), .D1(D1), .D2(D2), .D3(D3), .D4(D4), .D5(D5), .D6(D6),
    .D7(D7));

  // Notes on the sheet:
  //   A0: pin 10
  //   A1: pin 9
  //   A2: pin 8
  //   A3: pin 7
  //   A4: pin 6
  //   A5: pin 5
  //   A6: pin 4
  //   A7: pin 3
  //   A8: pin 25
  //   A9: pin 24
  //   A10: pin 21
  //   A11: pin 23
  //   A12: pin 2
  //   nCE: pin 20, default 1
  //   nOE: pin 22, default 1
  //   nWE: pin 27, default 1
  //   D0: pin 11
  //   D1: pin 12
  //   D2: pin 13
  //   D3: pin 15
  //   D4: pin 16
  //   D5: pin 17
  //   D6: pin 18
  //   D7: pin 19
  //   VCC: pin 28, default 1
  //   GND: pin 14
endmodule
