// Digital circuit Register.dig as structural Verilog
// Register module.
module Register (
  input  CLOCK,
  input  nIN,
  input  nOUT,
  output [7:0] BUS,
  output [7:0] OUT
);

  wire _74245_1_pin2, _74245_1_pin3, _74245_1_pin4, _74245_1_pin5, _74245_1_pin6, _74245_1_pin7,
       _74245_1_pin8, _74245_1_pin9;

  _74245 _74245_1 (
    .pin1(1'b0), .pin2(_74245_1_pin2), .pin3(_74245_1_pin3), .pin4(_74245_1_pin4), .pin5(_74245_1_pin5),
    .pin6(_74245_1_pin6), .pin7(_74245_1_pin7), .pin8(_74245_1_pin8), .pin9(_74245_1_pin9), .pin10(1'b0),
    .pin11(OUT[7]), .pin12(OUT[6]), .pin13(OUT[5]), .pin14(OUT[4]), .pin15(OUT[3]), .pin16(OUT[2]),
    .pin17(OUT[1]), .pin18(OUT[0]), .pin19(nOUT), .pin20(1'b1));
  BusSplitter #(.Bits(8)) bussplitter_1 (
    .D(BUS), .OE(nOUT), .D0(_74245_1_pin2), .D1(_74245_1_pin3), .D2(_74245_1_pin4), .D3(_74245_1_pin5),
    .D4(_74245_1_pin6), .D5(_74245_1_pin7), .D6(_74245_1_pin8), .D7(_74245_1_pin9));
  _74377 _74377_1 (
    .pin1(nIN), .pin2(OUT[0]), .pin3(BUS[0]), .pin4(BUS[1]), .pin5(OUT[1]), .pin6(OUT[2]), .pin7(BUS[2]),
    .pin8(BUS[3]), .pin9(OUT[3]), .pin10(1'b0), .pin11(CLOCK), .pin12(OUT[4]), .pin13(BUS[4]),
    .pin14(BUS[5]), .pin15(OUT[5]), .pin16(OUT[6]), .pin17(BUS[6]), .pin18(BUS[7]), .pin19(OUT[7]),
    .pin20(1'b1));

  // Other names for the same wires on the sheet: D0 = BUS[0]; D1 = BUS[1]; D2 = BUS[2]; D3 = BUS[3]; D4 = BUS[4];
  //   D5 = BUS[5]; D6 = BUS[6]; D7 = BUS[7]; Q0 = OUT[0]; Q1 = OUT[1]; Q2 = OUT[2]; Q3 = OUT[3]; Q4 = OUT[4];
  //   Q5 = OUT[5]; Q6 = OUT[6]; Q7 = OUT[7]; REG_IN = nIN; REG_OUT = nOUT

  // Notes on the sheet:
  //   nIN: default 1
  //   nOUT: default 1
  //   B to A (LOW)
  //   Digital workaround for bus sharing
endmodule
